# Fritzing sketch EspaceGam_chrono (saved by Fritzing 0.9.3b)
breadboards: 1

parts:
  8x8_LED_Modul_mit_MAX4 = 8x8 LED Modul mit MAX7219 [package=THT]
  Composant1 = Arduino Uno (Rev3)
  8x8_LED_Modul_mit_MAX5 = 8x8 LED Modul mit MAX7219 [package=THT]  # not connected
  8x8_LED_Modul_mit_MAX6 = 8x8 LED Modul mit MAX7219 [package=THT]  # not connected
  8x8_LED_Modul_mit_MAX7 = 8x8 LED Modul mit MAX7219 [package=THT]  # not connected
  BT1 = Bluetooth HC-06d [package=THT]
  Pause_button = Round Pushbutton
  R1 = Resistor [tolerance=±5% resistance=1k package="1206 [SMD]"]
  Start/Restart_Button = Round Pushbutton
  R2 = Resistor [tolerance=±5% resistance=1k package="1206 [SMD]"]

nets:
  5V: 8x8_LED_Modul_mit_MAX4.VCC_Eingang, Composant1.5V, BT1.VCC, Pause_button.leg1
  GND: 8x8_LED_Modul_mit_MAX4.GND_Eingang, Composant1.GND, BT1.GND, R1.Pin_1
  N1: 8x8_LED_Modul_mit_MAX4.DIN_Eingang, Composant1.D13/SCK
  N2: 8x8_LED_Modul_mit_MAX4.CS_Eingang, Composant1.D12/MISO
  N3: 8x8_LED_Modul_mit_MAX4.CLK_Eingang, Composant1.D11_PWM/MOSI
  N4: Composant1.D8, Start/Restart_Button.leg1, R2.Pin_1
  N5: Composant1.D9_PWM, BT1.TXD
  N6: Composant1.D10_PWM/SS, BT1.RXD
  N7: Composant1.D7, Pause_button.leg0, R1.Pin_0

custom parts:
  Bluetooth HC-06d: Bluetooth HC-06 - face down, pins down 16.5mm x 37.5mm PCB
