# Fritzing sketch Feurouge (saved by Fritzing 0.9.3b)
breadboards: 1

parts:
  R1 = Resistor [tolerance=±5% resistance=220 package=THT]
  R2 = Resistor [tolerance=±5% resistance=220 package=THT]
  R3 = Resistor [tolerance=±5% resistance=220 package=THT]
  Part1 = Arduino Uno (Rev3)
  LED1 = LED - 5mm [color="Red (633nm)" package="5 mm [THT]"]
  LED2 = LED - 5mm [color="Yellow (595nm)" package="5 mm [THT]"]
  LED3 = LED - 5mm [color="Green (555nm)" package="5 mm [THT]"]

nets:
  N1: R1.Pin_0, LED1.anode
  N2: R1.Pin_1, R2.Pin_1, R3.Pin_1, Part1.GND
  N3: R2.Pin_0, LED2.anode
  N4: R3.Pin_0, LED3.anode
  N5: Part1.D9_PWM, LED2.cathode
  N6: Part1.D12/MISO, LED3.cathode
  N7: Part1.D7, LED1.cathode
