# Fritzing sketch MouvementMelodie (saved by Fritzing 0.9.3b)
breadboards: 1

parts:
  Part1 = Arduino Uno (Rev3)
  R1 = Resistor [tolerance=±5% resistance=220 package=THT]
  LED1 = LED - 5mm [color="White (4500K)" package="5 mm [THT]"]
  R2 = Trimmer Potentiometer [maximum_resistance=10kΩ package=THT]
  J1 = Piezo Speaker
  Part2 = SRF05 Ultrasonic Rangefinder

nets:
  N1: Part1.A0, R2.wiper
  N2: Part1.D9_PWM, J1.pin2
  N3: Part1.D6_PWM, Part2.connector10
  N4: Part1.D7, Part2.connector9
  N5: Part1.5V, R2.leg1, Part2.connector8
  N6: Part1.GND, R2.leg2, J1.pin1, Part2.connector11
  N7: R1.Pin_0, LED1.anode
