# Fritzing sketch Relay (saved by Fritzing 0.9.3b)
breadboards: 1

parts:
  1Sheeld1 = 1Sheeld
  Part1 = Arduino Uno (Rev3)
  U1 = RELAY [package=relay-jzc]  # not connected

nets:
  N1: 1Sheeld1.D8, Part1.D7

custom parts:
  1Sheeld: 1Sheeld is a new easily configured shield for Arduino. It is connected to a mobile app that allow the usage of all of Android smartphones' capabilities such as LCD Screen, Gyroscope, Switches, LEDs, Accelerometer, Magnetometer, GSM, Wi-Fi, GPS ...etc. into your Arduino sketch.
